// Logisim project PongV2.circ as structural Verilog: 2 circuits, main circuit main
module main (
  output [31:0] out_1
);

  wire and_4_out, button_5_out, button_6_out, button_7_out, button_8_out, cdm_8_1_p2, cdm_8_1_p4, cdm_8_1_p5,
       cdm_8_1_p6, cdm_8_1_p8, cdm_8_1_p9, cdm_8_1_p10, Clk, clock_1_out, clock_2_out, Code, comparator_2_eq,
       comparator_2_gt, comparator_2_lt, comparator_3_eq, comparator_3_gt, comparator_3_lt, comparator_4_eq,
       comparator_4_gt, comparator_4_lt, comparator_5_eq, comparator_5_gt, comparator_5_lt, data,
       decoder_2_out0, decoder_2_out1, decoder_3_out1, decoder_4_out0, decoder_10_out0, decoder_11_out0,
       decoder_12_out0, decoder_15_out0, I_O_Sel, IO_F8_out, IO_FA_out, IO_FB_out, IO_FC_out, IO_FD_out,
       IO_FE_out, IO_FF_out, mem, multiplexer_34_out, nand_1_out, nor_1_out, nor_2_out, not_1_out, not_2_out,
       not_3_out, not_4_out, not_5_out, not_6_out, not_7_out, or_3_out, or_5_out, or_7_out, or_8_out,
       P_Reset, pull_resistor_1_node, RAM, Rd_Wr, Reset, transistor_1_out, undriven;
  wire [3:0] button_2_out, I_O_Adr, LScore, register_1_q, register_1_q_2, RScore;
  wire [4:0] bitfinder_1_index;
  wire [6:0] Keyboard;
  wire [7:0] bit_extender_1_out, cdm_8_1_p7, cdm_8_1_p14, cdm_8_1_p15, controlled_buffer_6_out, I_O_Dat,
       Paddle_Out, register_3_q, register_4_q, register_5_q, register_8_q, register_9_q, shifter_5_out,
       shifter_8_out, shifter_11_out, shifter_12_out;
  wire [7:4] cdm_8_1_p13, register_6_q, register_7_q;
  wire [7:7] rs_latch_1_p3;
  wire [15:0] decoder_5_out0, decoder_6_out0, decoder_8_out0, decoder_9_out0;
  wire [31:0] BallX, BallY, controlled_buffer_3_out, LPad, multiplexer_1_out, multiplexer_2_out,
       multiplexer_3_out, multiplexer_4_out, multiplexer_5_out, multiplexer_6_out, multiplexer_7_out,
       multiplexer_8_out, multiplexer_9_out, multiplexer_10_out, multiplexer_11_out, multiplexer_12_out,
       multiplexer_13_out, multiplexer_14_out, multiplexer_15_out, multiplexer_16_out, multiplexer_17_out,
       multiplexer_18_out, multiplexer_19_out, multiplexer_20_out, multiplexer_21_out, multiplexer_22_out,
       multiplexer_23_out, multiplexer_24_out, multiplexer_25_out, multiplexer_26_out, multiplexer_27_out,
       multiplexer_28_out, multiplexer_29_out, multiplexer_30_out, multiplexer_31_out, multiplexer_32_out,
       multiplexer_33_out, or_1_out, or_2_out, shifter_1_out, shifter_2_out, shifter_3_out, shifter_6_out,
       shifter_7_out, shifter_9_out, shifter_10_out, xnor_1_out, xnor_2_out;

  Multiplexer #(.width(32), .enable("false")) multiplexer_1 (
    .in0({32{1'b0}}), .in1(BallY), .out(multiplexer_1_out), .sel(BallX[30]));
  Multiplexer #(.width(32), .enable("false")) multiplexer_2 (
    .in0({32{1'b0}}), .in1(BallY), .out(multiplexer_2_out), .sel(BallX[31]));
  Multiplexer #(.width(32), .enable("false")) multiplexer_3 (
    .in0({32{1'b0}}), .in1(BallY), .out(multiplexer_3_out), .sel(BallX[28]));
  Multiplexer #(.width(32), .enable("false")) multiplexer_4 (
    .in0({32{1'b0}}), .in1(BallY), .out(multiplexer_4_out), .sel(BallX[29]));
  Keyboard keyboard_1 (.clk(Clk), .data(Keyboard));  // open: re, clr, avail
  Multiplexer #(.width(32), .enable("false")) multiplexer_5 (
    .in0({32{1'b0}}), .in1(BallY), .out(multiplexer_5_out), .sel(BallX[27]));
  Multiplexer #(.width(32), .enable("false")) multiplexer_6 (
    .in0({32{1'b0}}), .in1(BallY), .out(multiplexer_6_out), .sel(BallX[25]));
  Multiplexer #(.width(32), .enable("false")) multiplexer_7 (
    .in0({32{1'b0}}), .in1(BallY), .out(multiplexer_7_out), .sel(BallX[26]));
  Multiplexer #(.width(32), .enable("false")) multiplexer_8 (
    .in0({32{1'b0}}), .in1(BallY), .out(multiplexer_8_out), .sel(BallX[24]));
  Multiplexer #(.width(32), .enable("false")) multiplexer_9 (
    .in0({32{1'b0}}), .in1(BallY), .out(multiplexer_9_out), .sel(BallX[22]));
  Multiplexer #(.width(32), .enable("false")) multiplexer_10 (
    .in0({32{1'b0}}), .in1(BallY), .out(multiplexer_10_out), .sel(BallX[23]));
  Hex_Digit_Display hex_digit_display_1 (.value(LScore));  // open: dp
  Multiplexer #(.width(32), .enable("false")) multiplexer_11 (
    .in0({32{1'b0}}), .in1(BallY), .out(multiplexer_11_out), .sel(BallX[20]));
  Multiplexer #(.width(32), .enable("false")) multiplexer_12 (
    .in0({32{1'b0}}), .in1(BallY), .out(multiplexer_12_out), .sel(BallX[21]));
  DotMatrix #(.matrixcols(32), .matrixrows(32)) dotmatrix_1 (
    .col0(or_1_out), .col1(multiplexer_1_out), .col2(multiplexer_4_out), .col3(multiplexer_3_out),
    .col4(multiplexer_5_out), .col5(multiplexer_7_out), .col6(multiplexer_6_out), .col7(multiplexer_8_out),
    .col8(multiplexer_10_out), .col9(multiplexer_9_out), .col10(multiplexer_12_out),
    .col11(multiplexer_11_out), .col12(multiplexer_13_out), .col13(multiplexer_15_out),
    .col14(multiplexer_14_out), .col15(multiplexer_16_out), .col16(multiplexer_17_out),
    .col17(multiplexer_18_out), .col18(multiplexer_19_out), .col19(multiplexer_20_out),
    .col20(multiplexer_21_out), .col21(multiplexer_23_out), .col22(multiplexer_22_out),
    .col23(multiplexer_24_out), .col24(multiplexer_25_out), .col25(multiplexer_26_out),
    .col26(multiplexer_28_out), .col27(multiplexer_27_out), .col28(multiplexer_29_out),
    .col29(multiplexer_30_out), .col30(multiplexer_31_out), .col31(or_2_out));
  assign or_1_out = LPad | multiplexer_2_out;  // OR_Gate or_1, 32 bits wide
  Multiplexer #(.width(32), .enable("false")) multiplexer_13 (
    .in0({32{1'b0}}), .in1(BallY), .out(multiplexer_13_out), .sel(BallX[19]));
  Multiplexer #(.width(32), .enable("false")) multiplexer_14 (
    .in0({32{1'b0}}), .in1(BallY), .out(multiplexer_14_out), .sel(BallX[17]));
  Multiplexer #(.width(32), .enable("false")) multiplexer_15 (
    .in0({32{1'b0}}), .in1(BallY), .out(multiplexer_15_out), .sel(BallX[18]));
  Multiplexer #(.width(32), .enable("false")) multiplexer_16 (
    .in0({32{1'b0}}), .in1(BallY), .out(multiplexer_16_out), .sel(BallX[16]));
  Multiplexer #(.width(32), .enable("false")) multiplexer_17 (
    .in0({32{1'b0}}), .in1(BallY), .out(multiplexer_17_out), .sel(BallX[15]));
  Multiplexer #(.width(32), .enable("false")) multiplexer_18 (
    .in0({32{1'b0}}), .in1(BallY), .out(multiplexer_18_out), .sel(BallX[14]));
  Hex_Digit_Display hex_digit_display_2 (.value(RScore));  // open: dp
  assign or_2_out = out_1 | multiplexer_32_out;  // OR_Gate or_2, 32 bits wide
  Multiplexer #(.width(32), .enable("false")) multiplexer_19 (
    .in0({32{1'b0}}), .in1(BallY), .out(multiplexer_19_out), .sel(BallX[13]));
  Multiplexer #(.width(32), .enable("false")) multiplexer_20 (
    .in0({32{1'b0}}), .in1(BallY), .out(multiplexer_20_out), .sel(BallX[12]));
  // Probe on cdm_8_1_p2
  // Probe on cdm_8_1_p4
  Button button_1 (.out(Reset));
  and and_1 (Clk, ~pull_resistor_1_node, clock_1_out);  // AND_Gate
  Pull_Resistor pull_resistor_1 (.node(pull_resistor_1_node));
  Clock clock_1 (.out(clock_1_out));
  Comparator comparator_1 (.a(cdm_8_1_p7), .b({8{1'b1}}), .eq(pull_resistor_1_node));  // open: gt, lt
  Multiplexer #(.width(32), .enable("false")) multiplexer_21 (
    .in0({32{1'b0}}), .in1(BallY), .out(multiplexer_21_out), .sel(BallX[11]));
  // Probe on cdm_8_1_p5
  // Probe on cdm_8_1_p6
  // Probe on cdm_8_1_p7
  and and_2 (I_O_Sel, not_2_out, Clk, data);
  Multiplexer #(.width(32), .enable("false")) multiplexer_22 (
    .in0({32{1'b0}}), .in1(BallY), .out(multiplexer_22_out), .sel(BallX[9]));
  Multiplexer #(.width(32), .enable("false")) multiplexer_23 (
    .in0({32{1'b0}}), .in1(BallY), .out(multiplexer_23_out), .sel(BallX[10]));
  // Probe on cdm_8_1_p8
  // Probe on cdm_8_1_p9
  Multiplexer #(.width(32), .enable("false")) multiplexer_24 (
    .in0({32{1'b0}}), .in1(BallY), .out(multiplexer_24_out), .sel(BallX[8]));
  Decoder #(.disabled(0)) decoder_1 (.out0(Code), .out1(data), .sel(cdm_8_1_p10), .en(mem));
  not not_1 (not_1_out, Rd_Wr);
  assign I_O_Dat = not_1_out ? cdm_8_1_p14 : 8'bz;  // Controlled_Buffer controlled_buffer_1
  // CdM_8 cdm_8_1: pin names not known; wires that end beside it: Clk, cdm_8_1_p2, Reset, cdm_8_1_p4, cdm_8_1_p5, cdm_8_1_p6, cdm_8_1_p7, cdm_8_1_p8, cdm_8_1_p9, cdm_8_1_p10, mem, Rd_Wr, {cdm_8_1_p13, I_O_Adr}, cdm_8_1_p14, cdm_8_1_p15
  assign cdm_8_1_p15 = Rd_Wr ? I_O_Dat : 8'bz;  // Controlled_Buffer controlled_buffer_2
  not not_2 (not_2_out, nand_1_out);
  nand nand_1 (nand_1_out, cdm_8_1_p13[7], cdm_8_1_p13[6], cdm_8_1_p13[5], cdm_8_1_p13[4]);
  and and_3 (RAM, nand_1_out, data);
  Multiplexer #(.width(32), .enable("false")) multiplexer_25 (
    .in0({32{1'b0}}), .in1(BallY), .out(multiplexer_25_out), .sel(BallX[7]));
  Multiplexer #(.width(32), .enable("false")) multiplexer_26 (
    .in0({32{1'b0}}), .in1(BallY), .out(multiplexer_26_out), .sel(BallX[6]));
  Multiplexer #(.width(32), .enable("false")) multiplexer_27 (
    .in0({32{1'b0}}), .in1(BallY), .out(multiplexer_27_out), .sel(BallX[4]));
  Multiplexer #(.width(32), .enable("false")) multiplexer_28 (
    .in0({32{1'b0}}), .in1(BallY), .out(multiplexer_28_out), .sel(BallX[5]));
  // Probe on {cdm_8_1_p13, I_O_Adr}
  Multiplexer #(.width(32), .enable("false")) multiplexer_29 (
    .in0({32{1'b0}}), .in1(BallY), .out(multiplexer_29_out), .sel(BallX[3]));
  ROM rom_1 (.addr({cdm_8_1_p13, I_O_Adr}), .data(I_O_Dat), .sel(Code));
  RAM ram_1 (.addr({cdm_8_1_p13, I_O_Adr}), .data(I_O_Dat), .sel(RAM), .clk(Clk), .ld(Rd_Wr));  // open: clr
  Multiplexer #(.width(32), .enable("false")) multiplexer_30 (
    .in0({32{1'b0}}), .in1(BallY), .out(multiplexer_30_out), .sel(BallX[2]));
  Multiplexer #(.width(32), .enable("false")) multiplexer_31 (
    .in0({32{1'b0}}), .in1(BallY), .out(multiplexer_31_out), .sel(BallX[1]));
  Multiplexer #(.width(32), .enable("false")) multiplexer_32 (
    .in0({32{1'b0}}), .in1(BallY), .out(multiplexer_32_out), .sel(BallX[0]));
  // Probe on I_O_Dat
  Decoder #(.disabled(0)) decoder_2 (.out0(decoder_2_out0), .out1(decoder_2_out1), .sel(Rd_Wr), .en(and_4_out));
  Button button_2 (.out(button_2_out[0]));
  Button button_3 (.out(button_2_out[1]));
  and and_4 (and_4_out, I_O_Sel, I_O_Adr[0], I_O_Adr[1], ~I_O_Adr[2], ~I_O_Adr[3]);  // AND_Gate
  Hex_Digit_Display hex_digit_display_3 (.value(register_1_q));  // open: dp
  Shifter #(.width(32)) shifter_1 (.in(out_1), .\dist (5'b00001), .out(shifter_1_out));
  Shifter #(.width(32), .shift("lr")) shifter_2 (.in(out_1), .\dist (5'b00001), .out(shifter_2_out));
  Register register_1 (.D(I_O_Dat), .Q({register_1_q, register_1_q_2}), .clk(decoder_2_out0));  // open: en, clr
  Hex_Digit_Display hex_digit_display_4 (.value(register_1_q_2));  // open: dp
  assign controlled_buffer_3_out = not_3_out ? multiplexer_33_out : 32'bz;  // Controlled_Buffer controlled_buffer_3
  Multiplexer #(.select(4), .width(32), .enable("false")) multiplexer_33 (
    .in0(out_1), .in1(shifter_1_out), .in2(shifter_2_out), .in5(shifter_1_out), .in6(out_1), .in9(out_1),
    .in10(shifter_2_out), .out(multiplexer_33_out), .sel(button_2_out));  // open: in3, in4, in7, in8, in11, in12, in13, in14, in15
  not not_3 (not_3_out, P_Reset);
  assign controlled_buffer_3_out = P_Reset ? 32'h1c000 : 32'bz;  // Controlled_Buffer controlled_buffer_4
  Clock #(.lowDuration(16)) clock_2 (.out(clock_2_out));
  Button button_4 ();  // open: out
  assign I_O_Dat = decoder_2_out1 ? {rs_latch_1_p3[7], register_3_q[6:0]} : 8'bz;  // Controlled_Buffer controlled_buffer_5
  Register #(.width(32), .trigger("falling")) register_2 (
    .D(controlled_buffer_3_out), .Q(out_1), .clk(multiplexer_34_out));  // open: en, clr
  Multiplexer #(.disabled(0), .enable("false")) multiplexer_34 (
    .in0(clock_2_out), .in1(Clk), .out(multiplexer_34_out), .sel(P_Reset));
  Shifter #(.width(32)) shifter_3 (.in(out_1), .\dist (5'b00001), .out(shifter_3_out));
  assign xnor_1_out = ~(32'hf0000000 ^ out_1);  // XNOR_Gate xnor_1, 32 bits wide
  assign xnor_2_out = ~(32'hf ^ out_1);  // XNOR_Gate xnor_2, 32 bits wide
  Button button_5 (.out(button_5_out));
  assign controlled_buffer_6_out = button_5_out ? 8'h61 : 8'bz;  // Controlled_Buffer controlled_buffer_6
  not not_4 (not_4_out, transistor_1_out);
  not not_5 (not_5_out, decoder_2_out1);
  // Probe on bitfinder_1_index
  BitFinder #(.width(32)) bitfinder_1 (.in(shifter_3_out), .index(bitfinder_1_index));  // open: found
  and and_5 (button_2_out[3], xnor_1_out[29], xnor_1_out[30], xnor_1_out[31]);
  and and_6 (button_2_out[2], xnor_2_out[0], xnor_2_out[1], xnor_2_out[2]);
  Button button_6 (.out(button_6_out));
  Transistor #(.\type ("n")) transistor_1 (.in(1'b0), .out(transistor_1_out), .gate(button_6_out));
  Transistor #(.\type ("n")) transistor_2 (.in(1'b0), .out(transistor_1_out), .gate(button_5_out));
  assign controlled_buffer_6_out = button_6_out ? 8'h62 : 8'bz;  // Controlled_Buffer controlled_buffer_7
  nor nor_1 (nor_1_out, transistor_1_out, not_4_out);
  nor nor_2 (nor_2_out, decoder_2_out1, not_5_out);
  assign bit_extender_1_out = {{3{1'b0}}, bitfinder_1_index};  // Bit_Extender bit_extender_1
  Button button_7 (.out(button_7_out));
  Transistor #(.\type ("n")) transistor_3 (.in(1'b0), .out(transistor_1_out), .gate(button_7_out));
  assign controlled_buffer_6_out = button_7_out ? 8'h63 : 8'bz;  // Controlled_Buffer controlled_buffer_8
  // RS_latch rs_latch_1: pin names not known; wires that end beside it: nor_1_out, nor_2_out, rs_latch_1_p3[7]
  // Probe on Paddle_Out
  Shifter shifter_4 (.in(bit_extender_1_out), .\dist (3'b011), .out(Paddle_Out));
  Button button_8 (.out(button_8_out));
  Transistor #(.\type ("n")) transistor_4 (.in(1'b0), .out(transistor_1_out), .gate(button_8_out));
  assign controlled_buffer_6_out = button_8_out ? 8'h64 : 8'bz;  // Controlled_Buffer controlled_buffer_9
  not not_6 (not_6_out, not_7_out);
  Pull_Resistor #(.pull(1)) pull_resistor_2 (.node(transistor_1_out));
  not not_7 (not_7_out, transistor_1_out);
  Register #(.trigger("falling")) register_3 (
    .D(controlled_buffer_6_out), .Q(register_3_q), .clk(not_6_out));  // open: en, clr
  assign I_O_Dat = decoder_3_out1 ? Paddle_Out : 8'bz;  // Controlled_Buffer controlled_buffer_10
  and IO_F8 (IO_F8_out, I_O_Sel, ~I_O_Adr[0], ~I_O_Adr[1], ~I_O_Adr[2], I_O_Adr[3]);  // AND_Gate
  Decoder #(.disabled(0)) decoder_3 (.out1(decoder_3_out1), .sel(Rd_Wr), .en(IO_F8_out));  // open: out0
  and IO_FA (IO_FA_out, I_O_Sel, ~I_O_Adr[0], I_O_Adr[1], ~I_O_Adr[2], I_O_Adr[3]);  // AND_Gate
  Register register_4 (.D(I_O_Dat), .Q(register_4_q), .clk(decoder_4_out0));  // open: en, clr
  // Probe on register_4_q
  Shifter #(.shift("lr")) shifter_5 (.in(register_4_q), .\dist (3'b011), .out(shifter_5_out));
  Decoder #(.disabled(0)) decoder_4 (.out0(decoder_4_out0), .sel(Rd_Wr), .en(IO_FA_out));  // open: out1
  // Probe on shifter_5_out
  Comparator #(.mode("unsigned")) comparator_2 (
    .a(register_4_q), .b(8'h7f), .gt(comparator_2_gt), .eq(comparator_2_eq), .lt(comparator_2_lt));
  // Probe on shifter_5_out[3:0]
  or or_3 (or_3_out, comparator_2_gt, comparator_2_eq);
  // Probe on shifter_5_out[3:0]
  Decoder #(.select(4), .disabled(0)) decoder_5 (
    .out0(decoder_5_out0[0]), .out1(decoder_5_out0[1]), .out2(decoder_5_out0[2]), .out3(decoder_5_out0[3]),
    .out4(decoder_5_out0[4]), .out5(decoder_5_out0[5]), .out6(decoder_5_out0[6]), .out7(decoder_5_out0[7]),
    .out8(decoder_5_out0[8]), .out9(decoder_5_out0[9]), .out10(decoder_5_out0[10]),
    .out11(decoder_5_out0[11]), .out12(decoder_5_out0[12]), .out13(decoder_5_out0[13]),
    .out14(decoder_5_out0[14]), .out15(decoder_5_out0[15]), .sel(shifter_5_out[3:0]), .en(comparator_2_lt));
  Decoder #(.select(4), .disabled(0)) decoder_6 (
    .out0(decoder_6_out0[0]), .out1(decoder_6_out0[1]), .out2(decoder_6_out0[2]), .out3(decoder_6_out0[3]),
    .out4(decoder_6_out0[4]), .out5(decoder_6_out0[5]), .out6(decoder_6_out0[6]), .out7(decoder_6_out0[7]),
    .out8(decoder_6_out0[8]), .out9(decoder_6_out0[9]), .out10(decoder_6_out0[10]),
    .out11(decoder_6_out0[11]), .out12(decoder_6_out0[12]), .out13(decoder_6_out0[13]),
    .out14(decoder_6_out0[14]), .out15(decoder_6_out0[15]), .sel(shifter_5_out[3:0]), .en(or_3_out));
  // Probe on {decoder_6_out0, decoder_5_out0}
  Shifter #(.width(32)) shifter_6 (.in({decoder_6_out0, decoder_5_out0}), .\dist (5'b00001), .out(shifter_6_out));
  Shifter #(.width(32), .shift("lr")) shifter_7 (
    .in({decoder_6_out0, decoder_5_out0}), .\dist (5'b00001), .out(shifter_7_out));
  assign LPad = {decoder_6_out0, decoder_5_out0} | shifter_7_out | shifter_6_out;  // OR_Gate or_4, 32 bits wide
  and IO_FB (IO_FB_out, I_O_Sel, I_O_Adr[0], I_O_Adr[1], ~I_O_Adr[2], I_O_Adr[3]);  // AND_Gate
  Register register_5 (.D(I_O_Dat), .Q(register_5_q), .clk(undriven));  // open: en, clr
  // Probe on register_5_q
  Shifter #(.shift("lr")) shifter_8 (.in(register_5_q), .\dist (3'b011), .out(shifter_8_out));
  Decoder #(.disabled(0)) decoder_7 (.out0(P_Reset), .sel(Rd_Wr), .en(IO_FB_out));  // open: out1
  // Probe on shifter_8_out
  Comparator #(.mode("unsigned")) comparator_3 (
    .a(register_5_q), .b(8'h7f), .gt(comparator_3_gt), .eq(comparator_3_eq), .lt(comparator_3_lt));
  // Probe on shifter_8_out[3:0]
  or or_5 (or_5_out, comparator_3_gt, comparator_3_eq);
  // Probe on shifter_8_out[3:0]
  Decoder #(.select(4), .disabled(0)) decoder_8 (
    .out0(decoder_8_out0[0]), .out1(decoder_8_out0[1]), .out2(decoder_8_out0[2]), .out3(decoder_8_out0[3]),
    .out4(decoder_8_out0[4]), .out5(decoder_8_out0[5]), .out6(decoder_8_out0[6]), .out7(decoder_8_out0[7]),
    .out8(decoder_8_out0[8]), .out9(decoder_8_out0[9]), .out10(decoder_8_out0[10]),
    .out11(decoder_8_out0[11]), .out12(decoder_8_out0[12]), .out13(decoder_8_out0[13]),
    .out14(decoder_8_out0[14]), .out15(decoder_8_out0[15]), .sel(shifter_8_out[3:0]), .en(comparator_3_lt));
  Decoder #(.select(4), .disabled(0)) decoder_9 (
    .out0(decoder_9_out0[0]), .out1(decoder_9_out0[1]), .out2(decoder_9_out0[2]), .out3(decoder_9_out0[3]),
    .out4(decoder_9_out0[4]), .out5(decoder_9_out0[5]), .out6(decoder_9_out0[6]), .out7(decoder_9_out0[7]),
    .out8(decoder_9_out0[8]), .out9(decoder_9_out0[9]), .out10(decoder_9_out0[10]),
    .out11(decoder_9_out0[11]), .out12(decoder_9_out0[12]), .out13(decoder_9_out0[13]),
    .out14(decoder_9_out0[14]), .out15(decoder_9_out0[15]), .sel(shifter_8_out[3:0]), .en(or_5_out));
  // Probe on {decoder_9_out0, decoder_8_out0}
  Shifter #(.width(32)) shifter_9 (.in({decoder_9_out0, decoder_8_out0}), .\dist (5'b00001), .out(shifter_9_out));
  Shifter #(.width(32), .shift("lr")) shifter_10 (
    .in({decoder_9_out0, decoder_8_out0}), .\dist (5'b00001), .out(shifter_10_out));
  // OR_Gate or_6 has open pins: in0={decoder_9_out0, decoder_8_out0}, in1=shifter_10_out, in2=shifter_9_out, out=open
  Register register_6 (.D(I_O_Dat), .Q({register_6_q, LScore}), .clk(decoder_10_out0));  // open: en, clr
  and IO_FC (IO_FC_out, I_O_Sel, ~I_O_Adr[0], ~I_O_Adr[1], I_O_Adr[2], I_O_Adr[3]);  // AND_Gate
  Hex_Digit_Display hex_digit_display_5 (.value(LScore));  // open: dp
  Decoder #(.disabled(0)) decoder_10 (.out0(decoder_10_out0), .sel(Rd_Wr), .en(IO_FC_out));  // open: out1
  Register register_7 (.D(I_O_Dat), .Q({register_7_q, RScore}), .clk(decoder_11_out0));  // open: en, clr
  Hex_Digit_Display hex_digit_display_6 (.value(RScore));  // open: dp
  and IO_FD (IO_FD_out, I_O_Sel, I_O_Adr[0], ~I_O_Adr[1], I_O_Adr[2], I_O_Adr[3]);  // AND_Gate
  Decoder #(.disabled(0)) decoder_11 (.out0(decoder_11_out0), .sel(Rd_Wr), .en(IO_FD_out));  // open: out1
  Register register_8 (.D(I_O_Dat), .Q(register_8_q), .clk(decoder_12_out0));  // open: en, clr
  // Probe on register_8_q
  and IO_FE (IO_FE_out, I_O_Sel, ~I_O_Adr[0], I_O_Adr[1], I_O_Adr[2], I_O_Adr[3]);  // AND_Gate
  Decoder #(.disabled(0)) decoder_12 (.out0(decoder_12_out0), .sel(Rd_Wr), .en(IO_FE_out));  // open: out1
  // Probe on shifter_11_out
  Shifter #(.shift("lr")) shifter_11 (.in(register_8_q), .\dist (3'b011), .out(shifter_11_out));
  // Probe on shifter_11_out[3:0]
  Comparator #(.mode("unsigned")) comparator_4 (
    .a(register_8_q), .b(8'h7f), .gt(comparator_4_gt), .eq(comparator_4_eq), .lt(comparator_4_lt));
  // Probe on shifter_11_out[3:0]
  Decoder #(.select(4), .disabled(0)) decoder_13 (
    .out0(BallX[0]), .out1(BallX[1]), .out2(BallX[2]), .out3(BallX[3]), .out4(BallX[4]), .out5(BallX[5]),
    .out6(BallX[6]), .out7(BallX[7]), .out8(BallX[8]), .out9(BallX[9]), .out10(BallX[10]), .out11(BallX[11]),
    .out12(BallX[12]), .out13(BallX[13]), .out14(BallX[14]), .out15(BallX[15]), .sel(shifter_11_out[3:0]),
    .en(comparator_4_lt));
  Decoder #(.select(4), .disabled(0)) decoder_14 (
    .out0(BallX[16]), .out1(BallX[17]), .out2(BallX[18]), .out3(BallX[19]), .out4(BallX[20]),
    .out5(BallX[21]), .out6(BallX[22]), .out7(BallX[23]), .out8(BallX[24]), .out9(BallX[25]),
    .out10(BallX[26]), .out11(BallX[27]), .out12(BallX[28]), .out13(BallX[29]), .out14(BallX[30]),
    .out15(BallX[31]), .sel(shifter_11_out[3:0]), .en(or_7_out));
  or or_7 (or_7_out, comparator_4_gt, comparator_4_eq);
  // Probe on BallX
  and IO_FF (IO_FF_out, I_O_Sel, I_O_Adr[0], I_O_Adr[1], I_O_Adr[2], I_O_Adr[3]);
  Register register_9 (.D(I_O_Dat), .Q(register_9_q), .clk(decoder_15_out0));  // open: en, clr
  // Probe on register_9_q
  Shifter #(.shift("lr")) shifter_12 (.in(register_9_q), .\dist (3'b011), .out(shifter_12_out));
  Decoder #(.disabled(0)) decoder_15 (.out0(decoder_15_out0), .sel(Rd_Wr), .en(IO_FF_out));  // open: out1
  // Probe on shifter_12_out
  Comparator #(.mode("unsigned")) comparator_5 (
    .a(register_9_q), .b(8'h7f), .gt(comparator_5_gt), .eq(comparator_5_eq), .lt(comparator_5_lt));
  // Probe on shifter_12_out[3:0]
  or or_8 (or_8_out, comparator_5_gt, comparator_5_eq);
  // Probe on shifter_12_out[3:0]
  Decoder #(.select(4), .disabled(0)) decoder_16 (
    .out0(BallY[0]), .out1(BallY[1]), .out2(BallY[2]), .out3(BallY[3]), .out4(BallY[4]), .out5(BallY[5]),
    .out6(BallY[6]), .out7(BallY[7]), .out8(BallY[8]), .out9(BallY[9]), .out10(BallY[10]), .out11(BallY[11]),
    .out12(BallY[12]), .out13(BallY[13]), .out14(BallY[14]), .out15(BallY[15]), .sel(shifter_12_out[3:0]),
    .en(comparator_5_lt));
  Decoder #(.select(4), .disabled(0)) decoder_17 (
    .out0(BallY[16]), .out1(BallY[17]), .out2(BallY[18]), .out3(BallY[19]), .out4(BallY[20]),
    .out5(BallY[21]), .out6(BallY[22]), .out7(BallY[23]), .out8(BallY[24]), .out9(BallY[25]),
    .out10(BallY[26]), .out11(BallY[27]), .out12(BallY[28]), .out13(BallY[29]), .out14(BallY[30]),
    .out15(BallY[31]), .sel(shifter_12_out[3:0]), .en(or_8_out));
  // Probe on BallY

  // Other names for the same wires on the sheet: RPad[31:0] = out_1

  // Notes on the sheet:
  //   Keyboard Input-W,S,x
  //   contents of rom_1 (hex, n*v repeats v):
  //   d0 f d1 e1 a4 d1 e2 a4 d0 80 d1 e3 a4 d1 e4 a4 d1 e5 a4 ee 1b ee 19 ee 15 ee 75 d0 dc b0 d1 0 a1 d0
  //   fc a1 d0 dd b0 a1 d0 fd a1 ee 2d d0 de d1 fd f5 a1 d0 fe a1 d0 df d1 fe f5 a1 d0 ff a1 ee a6 3f d0
  //   e1 b0 d1 e2 b5 7b e0 4d ee 4d d2 de bb d2 e0 ba a e0 59 3c ee 5a 1c d2 de a8 d2 fe a8 d2 df bb d2 e6
  //   ba a e0 6c 3d ee 6d 1d d2 df a9 d2 ff a9 ee 15 d0 de b0 d1 1 71 e0 84 d1 fe 71 e0 89 ee b7 d0 da b0
  //   ee 8e d0 db b0 ee 8e d2 df ba d1 8 39 16 71 e8 9a ee b7 72 e3 9f ee b7 d0 e0 b1 81 a1 ee b7 d0 da d2
  //   db d1 ff f5 a1 a9 d0 fa d2 fb a1 a9 ee 15 d0 f8 b0 d1 0 d2 1 d3 2 71 e0 c9 72 e0 d2 73 e0 e7 d0 da
  //   b1 a1 d0 fa a1 ee 41 d0 fa b0 d2 8 18 3 18 d1 ff 71 e8 c9 d0 da a3 d0 fa a3 ee 41 d0 fa b0 d2 f8 18
  //   3 18 d1 0 71 e3 c9 d0 da a3 d0 fa a3 ee 41 d4 80 80 80
  //   Test
  //   Paddle input -F8
  //   FA-Left Paddle
  //   FB-Right Paddle
  //   FC - Left Score
  //   FD - Right Score
  //   FE - Ball X
  //   FF - Ball Y
endmodule

module CDM8 (
);

  wire and_2_out, cdm_8_1_p2, cdm_8_1_p4, cdm_8_1_p5, cdm_8_1_p6, cdm_8_1_p7, cdm_8_1_p8, cdm_8_1_p9,
       cdm_8_1_p10, Clk, decoder_1_out0, decoder_1_out1, decoder_1_out2, decoder_1_out3, decoder_1_out4,
       decoder_1_out5, decoder_1_out6, decoder_1_out7, I_O_Sel, not_1_out, not_2_out, Rd_Wr, Reset;
  wire [2:0] I_O_Adr;
  wire [7:0] cdm_8_1_p13, cdm_8_1_p14, I_O_Dat;
  wire [7:3] cdm_8_1_p12;

  // Probe on cdm_8_1_p2
  Button button_1 (.out(Reset));
  Clock clock_1 (.out(Clk));
  Decoder #(.select(3)) decoder_1 (
    .out0(decoder_1_out0), .out1(decoder_1_out1), .out2(decoder_1_out2), .out3(decoder_1_out3),
    .out4(decoder_1_out4), .out5(decoder_1_out5), .out6(decoder_1_out6), .out7(decoder_1_out7),
    .sel(I_O_Adr), .en(I_O_Sel));
  // Probe on cdm_8_1_p4
  // Probe on cdm_8_1_p5
  // Probe on cdm_8_1_p6
  Keyboard keyboard_1 ();  // open: clk, re, clr, avail, data
  LED led_1 (.in(decoder_1_out0));
  LED led_2 (.in(decoder_1_out1));
  LED led_3 (.in(decoder_1_out2));
  LED led_4 (.in(decoder_1_out3));
  // Probe on cdm_8_1_p8
  // Probe on cdm_8_1_p7
  LED led_5 (.in(decoder_1_out4));
  LED led_6 (.in(decoder_1_out5));
  LED led_7 (.in(decoder_1_out6));
  LED led_8 (.in(decoder_1_out7));
  // Probe on cdm_8_1_p9
  not not_1 (not_1_out, Rd_Wr);
  // CdM_8 cdm_8_1: pin names not known; wires that end beside it: Clk, cdm_8_1_p2, Reset, cdm_8_1_p4, cdm_8_1_p5, cdm_8_1_p6, cdm_8_1_p7, cdm_8_1_p8, cdm_8_1_p9, cdm_8_1_p10, Rd_Wr, {cdm_8_1_p12, I_O_Adr}, cdm_8_1_p13, cdm_8_1_p14, Rd_Wr
  assign I_O_Dat = not_1_out ? cdm_8_1_p13 : 8'bz;  // Controlled_Buffer controlled_buffer_1
  assign cdm_8_1_p14 = Rd_Wr ? I_O_Dat : 8'bz;  // Controlled_Buffer controlled_buffer_2
  not not_2 (not_2_out, I_O_Sel);
  and and_1 (I_O_Sel, cdm_8_1_p10, cdm_8_1_p12[7], cdm_8_1_p12[6], cdm_8_1_p12[5], cdm_8_1_p12[4], cdm_8_1_p12[3]);
  // Probe on {cdm_8_1_p12, I_O_Adr}
  and and_2 (and_2_out, cdm_8_1_p10, not_2_out);
  // Probe on I_O_Dat
  RAM ram_1 (.addr({cdm_8_1_p12, I_O_Adr}), .data(I_O_Dat), .sel(and_2_out), .clk(Clk), .ld(Rd_Wr));  // open: clr
endmodule
