// Logisim project TvTennis.circ as structural Verilog: 10 circuits, main circuit main
module main (
  input  [29:0] Y_Axis,
  input  [31:0] X_Axis
);

  wire boundarydetectionl_1_out_2, boundarydetectionr_1_out_2, CHANGE_DIFFICULTY_out, DOWN_2_out, DOWN_3_out,
       DOWN_out, Lcollision, LEFT_out, not_1_out, or_3_out, or_4_out, or_5_out, Rcollision, RESET_2_out,
       Reset_3_out, Reset_4_out, RESET_5_out, RESET_6_out, RESET_7_out, RESET_8_out, RESET_DIFFICULTY_out,
       RESET_out, RIGHT_out, UP_2_out, UP_3_out, UP_out, vx_movement_2_direction_2;
  wire [3:0] scorecounter_1_score, scorecounter_2_score;
  wire [31:0] AI_output, AI_test, multiplexer_1_out, multiplexer_2_out, multiplexer_3_out, multiplexer_4_out,
       multiplexer_5_out, multiplexer_6_out, multiplexer_7_out, multiplexer_8_out, multiplexer_9_out,
       multiplexer_10_out, multiplexer_11_out, multiplexer_12_out, multiplexer_13_out, multiplexer_14_out,
       multiplexer_15_out, multiplexer_16_out, multiplexer_17_out, multiplexer_18_out, multiplexer_19_out,
       multiplexer_20_out, multiplexer_21_out, multiplexer_22_out, multiplexer_23_out, multiplexer_24_out,
       multiplexer_25_out, multiplexer_26_out, multiplexer_27_out, multiplexer_28_out, multiplexer_29_out,
       multiplexer_30_out, multiplexer_31_out, multiplexer_32_out, or_1_out, or_2_out, PLAYER_2_out_4,
       vx_movement_1_x_position, vx_movement_2_x_position, x_axis_move_1_out_4, y_axis_move_1_out_4;

  // Probe on vx_movement_1_x_position
  Button RESET_DIFFICULTY (.out(RESET_DIFFICULTY_out));
  Button CHANGE_DIFFICULTY (.out(CHANGE_DIFFICULTY_out));
  Multiplexer #(.width(32), .enable("false")) multiplexer_1 (
    .in0({32{1'b0}}), .in1(vx_movement_1_x_position), .out(multiplexer_1_out),
    .sel(vx_movement_2_x_position[30]));
  Multiplexer #(.width(32), .enable("false")) multiplexer_2 (
    .in0({32{1'b0}}), .in1(vx_movement_1_x_position), .out(multiplexer_2_out),
    .sel(vx_movement_2_x_position[31]));
  // Probe on AI_test
  aiPaddle AI (
    .Ball_Input(vx_movement_1_x_position), .Change_Difficulty(RESET_DIFFICULTY_out),
    .Reset_Difficulty(CHANGE_DIFFICULTY_out), .TEST(AI_test), .Reset(RESET_out), .Output(AI_output),
    .enable(not_1_out));
  Button RESET (.out(RESET_out));
  Button UP (.out(UP_out));
  Paddle_Shift paddle_shift_1 (.Up(UP_out), .Down(DOWN_out), .Reset(RESET_2_out));  // open: out_4
  Button DOWN (.out(DOWN_out));
  Button RESET_2 (.out(RESET_2_out));
  Multiplexer #(.width(32), .enable("false")) multiplexer_3 (
    .in0({32{1'b0}}), .in1(vx_movement_1_x_position), .out(multiplexer_3_out),
    .sel(vx_movement_2_x_position[29]));
  Multiplexer #(.width(32), .enable("false")) multiplexer_4 (
    .in0({32{1'b0}}), .in1(vx_movement_1_x_position), .out(multiplexer_4_out),
    .sel(vx_movement_2_x_position[28]));
  not not_1 (not_1_out, vx_movement_2_direction_2);
  // Probe on AI_output
  HitDetection hitdetection_1 (
    .Paddle_Position(AI_output), .Ball_Y_Axis(vx_movement_1_x_position),
    .X_Collision(vx_movement_2_x_position[30]), .out_4(Lcollision));
  Multiplexer #(.width(32), .enable("false")) multiplexer_5 (
    .in0({32{1'b0}}), .in1(vx_movement_1_x_position), .out(multiplexer_5_out),
    .sel(vx_movement_2_x_position[27]));
  // Probe on Lcollision
  Multiplexer #(.width(32), .enable("false")) multiplexer_6 (
    .in0({32{1'b0}}), .in1(vx_movement_1_x_position), .out(multiplexer_6_out),
    .sel(vx_movement_2_x_position[26]));
  Multiplexer #(.width(32), .enable("false")) multiplexer_7 (
    .in0({32{1'b0}}), .in1(vx_movement_1_x_position), .out(multiplexer_7_out),
    .sel(vx_movement_2_x_position[25]));
  ScoreCounter scorecounter_1 (.Score(scorecounter_1_score), .Reset(Reset_3_out), .Input(multiplexer_2_out));
  Button Reset_3 (.out(Reset_3_out));
  Multiplexer #(.width(32), .enable("false")) multiplexer_8 (
    .in0({32{1'b0}}), .in1(vx_movement_1_x_position), .out(multiplexer_8_out),
    .sel(vx_movement_2_x_position[24]));
  Hex_Digit_Display hex_digit_display_1 (.value(scorecounter_1_score));  // open: dp
  DotMatrix #(.matrixcols(32), .matrixrows(32)) dotmatrix_1 (
    .col0(or_1_out), .col1(multiplexer_1_out), .col2(multiplexer_3_out), .col3(multiplexer_4_out),
    .col4(multiplexer_5_out), .col5(multiplexer_6_out), .col6(multiplexer_7_out), .col7(multiplexer_8_out),
    .col8(multiplexer_9_out), .col9(multiplexer_10_out), .col10(multiplexer_12_out),
    .col11(multiplexer_11_out), .col12(multiplexer_13_out), .col13(multiplexer_15_out),
    .col14(multiplexer_14_out), .col15(multiplexer_16_out), .col16(multiplexer_18_out),
    .col17(multiplexer_17_out), .col18(multiplexer_20_out), .col19(multiplexer_19_out),
    .col20(multiplexer_21_out), .col21(multiplexer_22_out), .col22(multiplexer_23_out),
    .col23(multiplexer_24_out), .col24(multiplexer_26_out), .col25(multiplexer_25_out),
    .col26(multiplexer_27_out), .col27(multiplexer_28_out), .col28(multiplexer_29_out),
    .col29(multiplexer_30_out), .col30(multiplexer_31_out), .col31(or_2_out));
  assign or_1_out = AI_output | multiplexer_2_out;  // OR_Gate or_1, 32 bits wide
  Multiplexer #(.width(32), .enable("false")) multiplexer_9 (
    .in0({32{1'b0}}), .in1(vx_movement_1_x_position), .out(multiplexer_9_out),
    .sel(vx_movement_2_x_position[23]));
  Multiplexer #(.width(32), .enable("false")) multiplexer_10 (
    .in0({32{1'b0}}), .in1(vx_movement_1_x_position), .out(multiplexer_10_out),
    .sel(vx_movement_2_x_position[22]));
  Multiplexer #(.width(32), .enable("false")) multiplexer_11 (
    .in0({32{1'b0}}), .in1(vx_movement_1_x_position), .out(multiplexer_11_out),
    .sel(vx_movement_2_x_position[20]));
  Multiplexer #(.width(32), .enable("false")) multiplexer_12 (
    .in0({32{1'b0}}), .in1(vx_movement_1_x_position), .out(multiplexer_12_out),
    .sel(vx_movement_2_x_position[21]));
  Multiplexer #(.width(32), .enable("false")) multiplexer_13 (
    .in0({32{1'b0}}), .in1(vx_movement_1_x_position), .out(multiplexer_13_out),
    .sel(vx_movement_2_x_position[19]));
  Multiplexer #(.width(32), .enable("false")) multiplexer_14 (
    .in0({32{1'b0}}), .in1(vx_movement_1_x_position), .out(multiplexer_14_out),
    .sel(vx_movement_2_x_position[17]));
  Multiplexer #(.width(32), .enable("false")) multiplexer_15 (
    .in0({32{1'b0}}), .in1(vx_movement_1_x_position), .out(multiplexer_15_out),
    .sel(vx_movement_2_x_position[18]));
  Hex_Digit_Display hex_digit_display_2 (.value(scorecounter_2_score));  // open: dp
  ScoreCounter scorecounter_2 (.Score(scorecounter_2_score), .Reset(Reset_4_out), .Input(multiplexer_32_out));
  assign or_2_out = PLAYER_2_out_4 | multiplexer_32_out;  // OR_Gate or_2, 32 bits wide
  Multiplexer #(.width(32), .enable("false")) multiplexer_16 (
    .in0({32{1'b0}}), .in1(vx_movement_1_x_position), .out(multiplexer_16_out),
    .sel(vx_movement_2_x_position[16]));
  Button Reset_4 (.out(Reset_4_out));
  Multiplexer #(.width(32), .enable("false")) multiplexer_17 (
    .in0({32{1'b0}}), .in1(vx_movement_1_x_position), .out(multiplexer_17_out),
    .sel(vx_movement_2_x_position[14]));
  Multiplexer #(.width(32), .enable("false")) multiplexer_18 (
    .in0({32{1'b0}}), .in1(vx_movement_1_x_position), .out(multiplexer_18_out),
    .sel(vx_movement_2_x_position[15]));
  // Probe on PLAYER_2_out_4
  // Probe on Rcollision
  Multiplexer #(.width(32), .enable("false")) multiplexer_19 (
    .in0({32{1'b0}}), .in1(vx_movement_1_x_position), .out(multiplexer_19_out),
    .sel(vx_movement_2_x_position[12]));
  Multiplexer #(.width(32), .enable("false")) multiplexer_20 (
    .in0({32{1'b0}}), .in1(vx_movement_1_x_position), .out(multiplexer_20_out),
    .sel(vx_movement_2_x_position[13]));
  HitDetection hitdetection_2 (
    .Paddle_Position(PLAYER_2_out_4), .Ball_Y_Axis(vx_movement_1_x_position),
    .X_Collision(vx_movement_2_x_position[1]), .out_4(Rcollision));
  Multiplexer #(.width(32), .enable("false")) multiplexer_21 (
    .in0({32{1'b0}}), .in1(vx_movement_1_x_position), .out(multiplexer_21_out),
    .sel(vx_movement_2_x_position[11]));
  Multiplexer #(.width(32), .enable("false")) multiplexer_22 (
    .in0({32{1'b0}}), .in1(vx_movement_1_x_position), .out(multiplexer_22_out),
    .sel(vx_movement_2_x_position[10]));
  Multiplexer #(.width(32), .enable("false")) multiplexer_23 (
    .in0({32{1'b0}}), .in1(vx_movement_1_x_position), .out(multiplexer_23_out),
    .sel(vx_movement_2_x_position[9]));
  Button RESET_5 (.out(RESET_5_out));
  Paddle_Shift PLAYER_2 (.Up(UP_2_out), .Down(DOWN_2_out), .Reset(RESET_5_out), .out_4(PLAYER_2_out_4));
  Multiplexer #(.width(32), .enable("false")) multiplexer_24 (
    .in0({32{1'b0}}), .in1(vx_movement_1_x_position), .out(multiplexer_24_out),
    .sel(vx_movement_2_x_position[8]));
  Button UP_2 (.out(UP_2_out));
  Button DOWN_2 (.out(DOWN_2_out));
  Multiplexer #(.width(32), .enable("false")) multiplexer_25 (
    .in0({32{1'b0}}), .in1(vx_movement_1_x_position), .out(multiplexer_25_out),
    .sel(vx_movement_2_x_position[6]));
  Multiplexer #(.width(32), .enable("false")) multiplexer_26 (
    .in0({32{1'b0}}), .in1(vx_movement_1_x_position), .out(multiplexer_26_out),
    .sel(vx_movement_2_x_position[7]));
  Button RESET_6 (.out(RESET_6_out));
  Button RESET_7 (.out(RESET_7_out));
  Multiplexer #(.width(32), .enable("false")) multiplexer_27 (
    .in0({32{1'b0}}), .in1(vx_movement_1_x_position), .out(multiplexer_27_out),
    .sel(vx_movement_2_x_position[5]));
  Multiplexer #(.width(32), .enable("false")) multiplexer_28 (
    .in0({32{1'b0}}), .in1(vx_movement_1_x_position), .out(multiplexer_28_out),
    .sel(vx_movement_2_x_position[4]));
  Button LEFT (.out(LEFT_out));
  Button RIGHT (.out(RIGHT_out));
  Button UP_3 (.out(UP_3_out));
  Button DOWN_3 (.out(DOWN_3_out));
  Multiplexer #(.width(32), .enable("false")) multiplexer_29 (
    .in0({32{1'b0}}), .in1(vx_movement_1_x_position), .out(multiplexer_29_out),
    .sel(vx_movement_2_x_position[3]));
  X_axis_move x_axis_move_1 (.Up(LEFT_out), .Reset(RESET_6_out), .Down(RIGHT_out), .out_4(x_axis_move_1_out_4));
  Y_axis_move y_axis_move_1 (.Up(UP_3_out), .Reset(RESET_7_out), .Down(DOWN_3_out), .out_4(y_axis_move_1_out_4));
  Multiplexer #(.width(32), .enable("false")) multiplexer_30 (
    .in0({32{1'b0}}), .in1(vx_movement_1_x_position), .out(multiplexer_30_out),
    .sel(vx_movement_2_x_position[2]));
  Multiplexer #(.width(32), .enable("false")) multiplexer_31 (
    .in0({32{1'b0}}), .in1(vx_movement_1_x_position), .out(multiplexer_31_out),
    .sel(vx_movement_2_x_position[1]));
  Multiplexer #(.width(32), .enable("false")) multiplexer_32 (
    .in0({32{1'b0}}), .in1(vx_movement_1_x_position), .out(multiplexer_32_out),
    .sel(vx_movement_2_x_position[0]));
  vX_movement vx_movement_1 (
    .Reset(or_4_out), .Direction(or_5_out), .X_Position(vx_movement_1_x_position));  // open: direction_2
  vX_movement vx_movement_2 (
    .Reset(or_4_out), .Direction(or_3_out), .X_Position(vx_movement_2_x_position),
    .direction_2(vx_movement_2_direction_2));
  BoundaryDetectionR boundarydetectionr_1 (.Ball_X_Axis(vx_movement_2_x_position), .out_2(boundarydetectionr_1_out_2));
  Button RESET_8 (.out(RESET_8_out));
  BoundaryDetectionL boundarydetectionl_1 (.Ball_X_Axis(vx_movement_2_x_position), .out_2(boundarydetectionl_1_out_2));
  or or_3 (or_3_out, vx_movement_2_x_position[0], Rcollision, Lcollision, vx_movement_2_x_position[31]);
  or or_4 (or_4_out, boundarydetectionr_1_out_2, RESET_8_out, boundarydetectionl_1_out_2);
  or or_5 (or_5_out, vx_movement_1_x_position[31], vx_movement_1_x_position[0]);
  // CdM_8 cdm_8_1: pin names not known
  RAM ram_1 ();  // open: addr, data, sel, clk, ld, clr

  // Notes on the sheet:
  //   PLAYER 1
endmodule

module Paddle_Shift (
  input  Up,
  input  Reset,
  input  Down,
  output [31:0] out_4
);

  wire clock_1_out, not_1_out;
  wire [3:2] and_2_out;
  wire [31:0] controlled_buffer_1_out, multiplexer_1_out, shifter_1_out, shifter_2_out, xnor_1_out,
       xnor_2_out;

  Shifter #(.width(32)) shifter_1 (.in(out_4), .\dist (5'b00001), .out(shifter_1_out));
  Shifter #(.width(32), .shift("lr")) shifter_2 (.in(out_4), .\dist (5'b00001), .out(shifter_2_out));
  Multiplexer #(.select(4), .width(32), .enable("false")) multiplexer_1 (
    .in0(out_4), .in1(shifter_1_out), .in2(shifter_2_out), .in5(shifter_1_out), .in6(out_4), .in9(out_4),
    .in10(shifter_2_out), .out(multiplexer_1_out), .sel({and_2_out, Down, Up}));  // open: in3, in4, in7, in8, in11, in12, in13, in14, in15
  not not_1 (not_1_out, Reset);
  assign controlled_buffer_1_out = not_1_out ? multiplexer_1_out : 32'bz;  // Controlled_Buffer controlled_buffer_1
  Clock clock_1 (.out(clock_1_out));
  assign controlled_buffer_1_out = Reset ? 32'h1c000 : 32'bz;  // Controlled_Buffer controlled_buffer_2
  Register #(.width(32)) register_1 (.D(controlled_buffer_1_out), .Q(out_4), .clk(clock_1_out));  // open: en, clr
  assign xnor_1_out = ~(32'he0000000 ^ out_4);  // XNOR_Gate xnor_1, 32 bits wide
  and and_1 (and_2_out[3], xnor_1_out[29], xnor_1_out[30], xnor_1_out[31]);
  assign xnor_2_out = ~(32'h7 ^ out_4);  // XNOR_Gate xnor_2, 32 bits wide
  and and_2 (and_2_out[2], xnor_2_out[0], xnor_2_out[1], xnor_2_out[2]);
endmodule

module Y_axis_move (
  input  Up,
  input  Reset,
  input  Down,
  output [31:0] out_4
);

  wire clock_1_out, not_1_out;
  wire [31:0] controlled_buffer_1_out, multiplexer_1_out, shifter_1_out, shifter_2_out;

  Shifter #(.width(32)) shifter_1 (.in(out_4), .\dist (5'b00001), .out(shifter_1_out));
  Shifter #(.width(32), .shift("lr")) shifter_2 (.in(out_4), .\dist (5'b00001), .out(shifter_2_out));
  assign controlled_buffer_1_out = not_1_out ? multiplexer_1_out : 32'bz;  // Controlled_Buffer controlled_buffer_1
  Multiplexer #(.select(2), .width(32), .enable("false")) multiplexer_1 (
    .in0(out_4), .in1(shifter_1_out), .in2(shifter_2_out), .out(multiplexer_1_out), .sel({Down, Up}));  // open: in3
  not not_1 (not_1_out, Reset);
  Register #(.width(32)) register_1 (.D(controlled_buffer_1_out), .Q(out_4), .clk(clock_1_out));  // open: en, clr
  Clock clock_1 (.out(clock_1_out));
  assign controlled_buffer_1_out = Reset ? 32'h40000 : 32'bz;  // Controlled_Buffer controlled_buffer_2
endmodule

module X_axis_move (
  input  Up,
  input  Reset,
  input  Down,
  output [31:0] out_4
);

  wire clock_1_out, not_1_out;
  wire [31:0] controlled_buffer_1_out, multiplexer_1_out, shifter_1_out, shifter_2_out;

  Shifter #(.width(32)) shifter_1 (.in(out_4), .\dist (5'b00001), .out(shifter_1_out));
  Shifter #(.width(32), .shift("lr")) shifter_2 (.in(out_4), .\dist (5'b00001), .out(shifter_2_out));
  assign controlled_buffer_1_out = not_1_out ? multiplexer_1_out : 32'bz;  // Controlled_Buffer controlled_buffer_1
  Multiplexer #(.select(2), .width(32), .enable("false")) multiplexer_1 (
    .in0(out_4), .in1(shifter_1_out), .in2(shifter_2_out), .out(multiplexer_1_out), .sel({Down, Up}));  // open: in3
  not not_1 (not_1_out, Reset);
  Register #(.width(32)) register_1 (.D(controlled_buffer_1_out), .Q(out_4), .clk(clock_1_out));  // open: en, clr
  Clock clock_1 (.out(clock_1_out));
  assign controlled_buffer_1_out = Reset ? 32'h40000 : 32'bz;  // Controlled_Buffer controlled_buffer_2
endmodule

module ScoreCounter (
  input  Reset,
  input  [31:0] Input,
  output [3:0] Score
);

  wire or_1_out;
  wire [3:0] adder_1_out;

  Register #(.width(4)) register_1 (.D(adder_1_out), .Q(Score), .clk(or_1_out), .clr(Reset));  // open: en
  Adder #(.width(4)) adder_1 (.a(Score), .b(4'b0001), .out(adder_1_out));  // open: cin, cout
  or or_1 (or_1_out, Input[0], Input[1], Input[2], Input[3], Input[4], Input[5], Input[6], Input[7], Input[8], Input[9], Input[10], Input[11], Input[12], Input[13], Input[14], Input[15], Input[16], Input[17], Input[18], Input[19], Input[20], Input[21], Input[22], Input[23], Input[24], Input[25], Input[26], Input[27], Input[28], Input[29], Input[30], Input[31]);
endmodule

module HitDetection (
  input  [31:0] Paddle_Position,
  input  [31:0] Ball_Y_Axis,
  input  X_Collision,
  output out_4
);

  wire or_1_out;
  wire [31:0] and_1_out;

  assign and_1_out = Paddle_Position & Ball_Y_Axis;  // AND_Gate and_1, 32 bits wide
  or or_1 (or_1_out, and_1_out[0], and_1_out[1], and_1_out[2], and_1_out[3], and_1_out[4], and_1_out[5], and_1_out[6], and_1_out[7], and_1_out[8], and_1_out[9], and_1_out[10], and_1_out[11], and_1_out[12], and_1_out[13], and_1_out[14], and_1_out[15], and_1_out[16], and_1_out[17], and_1_out[18], and_1_out[19], and_1_out[20], and_1_out[21], and_1_out[22], and_1_out[23], and_1_out[24], and_1_out[25], and_1_out[26], and_1_out[27], and_1_out[28], and_1_out[29], and_1_out[30], and_1_out[31]);
  and and_2 (out_4, or_1_out, X_Collision);
endmodule

module vX_movement (
  input  Reset,
  input  Direction,
  output [31:0] X_Position,
  output direction_2
);

  wire clock_1_out, not_1_out;
  wire [31:0] controlled_buffer_1_out, multiplexer_1_out, shifter_1_out, shifter_2_out;

  T_Flip_Flop t_ff_1 (.clk(Direction), .T(1'b1), .Q(direction_2));  // open: Qn, preset, reset, en
  Shifter #(.width(32)) shifter_1 (.in(X_Position), .\dist (5'b00001), .out(shifter_1_out));
  Multiplexer #(.width(32), .enable("false")) multiplexer_1 (
    .in0(shifter_1_out), .in1(shifter_2_out), .out(multiplexer_1_out), .sel(direction_2));
  Shifter #(.width(32), .shift("lr")) shifter_2 (.in(X_Position), .\dist (5'b00001), .out(shifter_2_out));
  assign controlled_buffer_1_out = not_1_out ? multiplexer_1_out : 32'bz;  // Controlled_Buffer controlled_buffer_1
  not not_1 (not_1_out, Reset);
  Clock #(.highDuration(3)) clock_1 (.out(clock_1_out));
  assign controlled_buffer_1_out = Reset ? 32'h40000 : 32'bz;  // Controlled_Buffer controlled_buffer_2
  Register #(.width(32)) register_1 (.D(controlled_buffer_1_out), .Q(X_Position), .clk(clock_1_out));  // open: en, clr
endmodule

module BoundaryDetectionR (
  input  [31:0] Ball_X_Axis,
  output out_2
);

  wire [31:0] and_1_out;

  assign and_1_out = 32'h1 & Ball_X_Axis;  // AND_Gate and_1, 32 bits wide
  buf or_1 (out_2, and_1_out[0]);  // OR_Gate
endmodule

module BoundaryDetectionL (
  input  [31:0] Ball_X_Axis,
  output out_2
);

  wire [31:0] and_1_out;

  assign and_1_out = 32'h80000000 & Ball_X_Axis;  // AND_Gate and_1, 32 bits wide
  buf or_1 (out_2, and_1_out[31]);  // OR_Gate
endmodule

module aiPaddle (
  input  enable,
  input  Reset,
  input  [31:0] Ball_Input,
  input  Change_Difficulty,
  input  Reset_Difficulty,
  output [31:0] Output,
  output [31:0] TEST
);

  wire clock_1_out, clock_2_out, clock_3_out, clock_4_out, comparator_1_eq, controlled_buffer_7_out,
       multiplexer_2_out, not_1_out, not_2_out, not_3_out;
  wire [2:0] controlled_buffer_5_out, register_2_q, shifter_5_out;
  wire [3:0] comparator_1_lt, controlled_buffer_1_out;
  wire [4:0] bitfinder_1_index;
  wire [31:0] controlled_buffer_3_out, multiplexer_1_out, shifter_1_out, shifter_2_out, shifter_3_out,
       xnor_1_out, xnor_2_out;

  BitFinder #(.width(32)) bitfinder_1 (.in(Output), .index(bitfinder_1_index));  // open: found
  Comparator #(.width(32)) comparator_1 (
    .a(TEST), .b(Ball_Input), .gt(comparator_1_lt[1]), .eq(comparator_1_eq), .lt(comparator_1_lt[0]));
  Shifter #(.width(32), .shift("rl")) shifter_1 (.in(32'h80000000), .\dist (bitfinder_1_index), .out(shifter_1_out));
  Shifter #(.width(32)) shifter_2 (.in(Output), .\dist (5'b00001), .out(shifter_2_out));
  Shifter #(.width(32), .shift("lr")) shifter_3 (.in(Output), .\dist (5'b00001), .out(shifter_3_out));
  Shifter #(.width(32), .shift("rl")) shifter_4 (.in(shifter_1_out), .\dist (5'b00010), .out(TEST));
  Multiplexer #(.select(4), .width(32), .enable("false")) multiplexer_1 (
    .in0(Output), .in1(shifter_2_out), .in2(shifter_3_out), .in5(shifter_2_out), .in6(Output), .in9(Output),
    .in10(shifter_3_out), .out(multiplexer_1_out), .sel(controlled_buffer_1_out));  // open: in3, in4, in7, in8, in11, in12, in13, in14, in15
  assign controlled_buffer_1_out = comparator_1_eq ? 4'b0000 : 4'bz;  // Controlled_Buffer controlled_buffer_1
  assign controlled_buffer_1_out = not_1_out ? comparator_1_lt : 4'bz;  // Controlled_Buffer controlled_buffer_2
  not not_1 (not_1_out, comparator_1_eq);
  assign controlled_buffer_3_out = not_2_out ? multiplexer_1_out : 32'bz;  // Controlled_Buffer controlled_buffer_3
  not not_2 (not_2_out, Reset);
  assign controlled_buffer_3_out = Reset ? 32'h1c000 : 32'bz;  // Controlled_Buffer controlled_buffer_4
  Clock clock_1 (.out(clock_1_out));
  not not_3 (not_3_out, Change_Difficulty);
  assign controlled_buffer_5_out = not_3_out ? shifter_5_out : 3'bz;  // Controlled_Buffer controlled_buffer_5
  assign controlled_buffer_5_out = Change_Difficulty ? 3'b001 : 3'bz;  // Controlled_Buffer controlled_buffer_6
  Register #(.width(32)) register_1 (
    .D(controlled_buffer_3_out), .Q(Output), .clk(controlled_buffer_7_out));  // open: en, clr
  assign controlled_buffer_7_out = enable ? multiplexer_2_out : 1'bz;  // Controlled_Buffer controlled_buffer_7
  Multiplexer #(.select(3)) multiplexer_2 (
    .in0(clock_1_out), .in1(clock_1_out), .in2(clock_2_out), .in4(clock_3_out), .out(multiplexer_2_out),
    .sel(shifter_5_out), .en(1'b1));  // open: in3, in5, in6, in7
  Clock #(.highDuration(5)) clock_2 (.out(clock_2_out));
  Clock #(.highDuration(10)) clock_3 (.out(clock_3_out));
  Clock clock_4 (.out(clock_4_out));
  // Probe on shifter_5_out
  Register #(.width(3)) register_2 (.D(controlled_buffer_5_out), .Q(register_2_q), .clk(clock_4_out));  // open: en, clr
  Shifter #(.width(3), .shift("rl")) shifter_5 (
    .in(register_2_q), .\dist ({1'b0, Reset_Difficulty}), .out(shifter_5_out));
  assign xnor_1_out = ~(32'he0000000 ^ Output);  // XNOR_Gate xnor_1, 32 bits wide
  and and_1 (comparator_1_lt[3], xnor_1_out[29], xnor_1_out[30], xnor_1_out[31]);
  assign xnor_2_out = ~(32'h7 ^ Output);  // XNOR_Gate xnor_2, 32 bits wide
  and and_2 (comparator_1_lt[2], xnor_2_out[0], xnor_2_out[1], xnor_2_out[2]);
endmodule
